# Fritzing sketch LinearEncoderFakeNunchuk (saved by Fritzing 0.7.5b)

parts:
  Arduino1 = Arduino
  LinearEncoder = mystery part, 4 pins [chip_label="Lin. Encoder" spacing=300mil]
  VCC1 = Battery block 9V
  ExpansionConnector = mystery part, 6 pins [chip_label=ExpCon spacing=300mil]
  S1 = Toggle Switch [package=THT]

nets:
  N1: Arduino1.GND, LinearEncoder.pin4, VCC1.-, ExpansionConnector.pin4
  N2: Arduino1.D4, ExpansionConnector.pin2
  N3: Arduino1.D3, LinearEncoder.pin2
  N4: Arduino1.D2, LinearEncoder.pin1
  N5: Arduino1.+5V, LinearEncoder.pin3
  N6: Arduino1.VIN, S1.L1
  N7: Arduino1.SCL, ExpansionConnector.pin6
  N8: Arduino1.SDA, ExpansionConnector.pin3
  N9: VCC1.+, S1.COM

notes:
  Wiimote Expansion Cable:
  Connector Pinout
  SCL UNUSED GND
  VCC3.3 DevDetect SDA
  The mystery part below represents that connector.
  Power Switch
